// Digital circuit DataReady.dig as structural Verilog
module DataReady (
  input  nCE,
  input  CLK,
  input  [1:0] in_3,
  output nDTACK
);

  wire _74153_1_pin7, CE, DTACK, WAIT0, WAIT1, WAIT2, WAIT3;

  _74164 _74164_1 (
    .pin1(1'b1), .pin2(1'b1), .pin3(WAIT0), .pin4(WAIT1), .pin5(WAIT2), .pin6(WAIT3), .pin7(1'b0),
    .pin8(CLK), .pin9(CE), .pin14(1'b1));  // open: pin10, pin11, pin12, pin13
  not not_1 (CE, nCE);
  _74153 _74153_1 (
    .pin1(1'b0), .pin2(in_3[1]), .pin3(WAIT3), .pin4(WAIT2), .pin5(WAIT1), .pin6(WAIT0),
    .pin7(_74153_1_pin7), .pin8(1'b0), .pin10(1'b0), .pin11(1'b0), .pin12(1'b0), .pin13(1'b0),
    .pin14(in_3[0]), .pin15(1'b0), .pin16(1'b1));  // open: pin9
  not not_2 (DTACK, _74153_1_pin7);
  assign nDTACK = ~nCE ? DTACK : 1'bz;  // DriverInvSel driverinvsel_1

  // Other names for the same wires on the sheet: SEL0 = in_3[0]; SEL1 = in_3[1]
endmodule
